// Logisim project BinaryCounter.circ as structural Verilog: 1 circuit, main circuit main
module main (
  output [2:0] out_1
);

  wire and_1_out, and_2_out, clock_1_out;

  and and_1 (and_1_out, out_1[1], out_1[0], 1'b1);
  and and_2 (and_2_out, out_1[0], 1'b1);
  Clock clock_1 (.out(clock_1_out));
  T_Flip_Flop t_ff_1 (.clk(clock_1_out), .T(and_1_out), .Q(out_1[2]));  // open: Qn, preset, reset, en
  T_Flip_Flop t_ff_2 (.clk(clock_1_out), .T(and_2_out), .Q(out_1[1]));  // open: Qn, preset, reset, en
  T_Flip_Flop t_ff_3 (.clk(clock_1_out), .T(1'b1), .Q(out_1[0]));  // open: Qn, preset, reset, en
  // Probe on out_1
endmodule
